# Fritzing sketch Development-Connection (saved by Fritzing 0.9.4)

parts:
  U1 = XBEE-1 [package=xbee-1]
  IC1 = ATMEGA4809 Xplain Board [package="DIP (Dual Inline) [THT]"]
  U3 = POT [package=pot_alpha_rv16af-20]
  Part1 = SO-24x [chip_label=SO-24x package=SO(x)]  # not connected

nets:
  N1: U1.VDD, IC1.pin_320
  N2: U1.DOUT, IC1.pin_313
  N3: U1.DIN, IC1.pin_314
  N4: U1.DTR, U1.GND, IC1.pin_319
  N5: U1.CTS, IC1.pin_306
  N6: U1.RTS, IC1.pin_305
  N7: IC1.pin_503, U3.S
  N8: IC1.pin_519, U3.E
  N9: IC1.pin_520, U3.A

custom parts:
  ATMEGA4809 Xplain Board: A DIP stand-in part for whatever IC you want. With 8 pins on a 300mil dual inline package (DIP) footprint.
