# Fritzing sketch Development-Connection_1 (saved by Fritzing 0.9.4)
breadboards: 1

parts:
  U1 = XBEE-1 [package=xbee-1]
  IC1 = ATMEGA4809 Xplain Board [package="DIP (Dual Inline) [THT]"]
  R1 = TRIMPOT [package=trimpot_pth_s3_lock]

nets:
  N1: U1.VDD, IC1.pin_420
  N2: U1.DOUT, IC1.pin_313
  N3: U1.DIN, IC1.pin_314
  N4: U1.DTR, U1.GND, IC1.pin_419
  N5: IC1.pin_319, IC1.pin_320, R1.CCW
  N6: IC1.pin_503, R1.WIPER

custom parts:
  ATMEGA4809 Xplain Board: A DIP stand-in part for whatever IC you want. With 8 pins on a 300mil dual inline package (DIP) footprint.
